// Logisim project Adder Example.circ as structural Verilog: 1 circuit, main circuit main
module main (
  input  Carry_in,
  input  Input1,
  input  Input2,
  output Sum,
  output Carry_out
);

  wire AND_2_out, AND_out, XOR_out;

  xor XOR (XOR_out, Input1, Input2);
  and AND (AND_out, Carry_in, XOR_out);
  and AND_2 (AND_2_out, Input2, Input1);
  xor XOR_2 (Sum, XOR_out, Carry_in);
  or OR (Carry_out, AND_out, AND_2_out);
endmodule
