// Logisim project Multiplexer and Demultiplexer Example.circ as structural Verilog: 3 circuits, main circuit main
module main (
  input  Select1,
  input  Select2,
  input  Bit_1,
  input  Bit_2,
  input  Bit_3,
  input  Bit_4,
  output Bit_1_2,
  output Bit_2_2,
  output Bit_3_2,
  output Bit_3_3
);

  wire multiplexer_example_1_output;

  Multiplexer_Example multiplexer_example_1 (
    .Input1(Bit_1), .Input2(Bit_2), .Input3(Bit_3), .Input4(Bit_4), .Output(multiplexer_example_1_output),
    .Select1(Select1), .Select2(Select2));
  Demultiplexer_Example demultiplexer_example_1 (
    .Output1(Bit_1_2), .Output2(Bit_2_2), .Output3(Bit_3_2), .Output4(Bit_3_3),
    .Input(multiplexer_example_1_output), .Select1(Select1), .Select2(Select2));
endmodule

module Multiplexer_Example (
  input  Select1,
  input  Select2,
  input  Input1,
  input  Input2,
  input  Input3,
  input  Input4,
  output Output
);

  wire and_1_out, and_2_out, and_3_out, and_4_out, not_1_out, not_2_out;

  not not_1 (not_1_out, Select1);
  not not_2 (not_2_out, Select2);
  and and_1 (and_1_out, Input1, not_2_out, not_1_out);
  and and_2 (and_2_out, Input2, Select2, not_1_out);
  and and_3 (and_3_out, Input3, Select1, not_2_out);
  and and_4 (and_4_out, Input4, Select2, Select1);
  or or_1 (Output, and_1_out, and_2_out, and_3_out, and_4_out);

  // Notes on the sheet:
  //   Multiplexer
endmodule

module Demultiplexer_Example (
  input  Select1,
  input  Select2,
  input  Input,
  output Output1,
  output Output2,
  output Output3,
  output Output4
);

  wire not_1_out, not_2_out;

  not not_1 (not_1_out, Select1);
  not not_2 (not_2_out, Select2);
  and and_1 (Output1, Input, not_2_out, not_1_out);
  and and_2 (Output2, Input, Select2, not_1_out);
  and and_3 (Output3, Input, Select1, not_2_out);
  and and_4 (Output4, Input, Select1, Select2);

  // Notes on the sheet:
  //   Demultiplexer
endmodule
